# Fritzing sketch diagram (saved by Fritzing 0.9.3b)
breadboards: 1

parts:
  Part1 = Arduino Uno (Rev3)
  VCC1 = 4 x AAA Battery Mount
  S1 = Pushbutton [package="[SMD]"]
  S2 = Pushbutton [package="[SMD]"]
  S3 = Pushbutton [package="[SMD]"]
  S4 = Pushbutton [package="[SMD]"]
  S5 = Pushbutton [package="[SMD]"]
  R1 = Resistor [tolerance=±5% resistance=220 package=THT]
  R7 = Resistor [tolerance=±5% resistance=220 package=THT]
  R8 = Resistor [tolerance=±5% resistance=220 package=THT]
  R9 = Resistor [tolerance=±5% resistance=220 package=THT]
  R10 = Resistor [tolerance=±5% resistance=220 package=THT]
  U1 = TA7291P [package=HSIP10-P-2.54(THT)]
  U2 = TA7291P [package=HSIP10-P-2.54(THT)]
  M1 = DC Motor
  M2 = DC Motor
  R11 = Resistor [tolerance=±5% resistance=220 package=THT]
  R12 = Resistor [tolerance=±5% resistance=220 package=THT]

nets:
  N1: Part1.D9_PWM, U2.IN2
  N2: Part1.D10_PWM/SS, U2.IN1
  N3: Part1.D0/RX, S5.Pin_1, S5.Pin_2, R1.Pin_0, R1.Pin_1
  N4: Part1.D1/TX, S4.Pin_1, S4.Pin_2, R7.Pin_0, R7.Pin_1
  N5: Part1.D2, S3.Pin_1, S3.Pin_2, R8.Pin_0, R8.Pin_1
  N6: Part1.D3_PWM, S2.Pin_1, S2.Pin_2, R9.Pin_0, R9.Pin_1
  N7: Part1.D4, S1.Pin_1, S1.Pin_2, R10.Pin_0, R10.Pin_1
  N8: Part1.D5_PWM, U1.IN2
  N9: Part1.D6_PWM, U1.IN1
  VCC: Part1.5V, U1.Vcc, U2.Vcc, R12.Pin_0
  GND: Part1.GND, VCC1.-, S1.Pin_3, S1.Pin_4, S2.Pin_3, S2.Pin_4, S3.Pin_3, S3.Pin_4, S4.Pin_3, S4.Pin_4, S5.Pin_3, S5.Pin_4, U1.GND, U2.GND, R11.Pin_0
  N10: VCC1.+, U1.Vs, U2.Vs
  N11: U1.OUT1, M2.pin_1
  N12: U1.Vref, R11.Pin_1
  N13: U1.OUT2, M2.pin_2
  N14: U2.OUT1, M1.pin_1
  N15: U2.Vref, R12.Pin_1
  N16: U2.OUT2, M1.pin_2

custom parts:
  TA7291P: The IC are Full-Bridge Driver. 4 modes available (CW / CCW / STOP / BRAKE) and PWM control. Output current:1.0 A (AVE.) 2.0 A (PEAK)
